// Logisim project Single Cycle Datapath.circ as structural Verilog: 20 circuits, main circuit 1 BIT ALU
// 1 ALU
module _1_BIT_ALU (
  input  A_invert,
  input  B_Invert,
  input  C_in,
  input  [1:0] Op_code,
  input  A,
  input  B,
  input  Less,
  output Result,
  output Set,
  output Overflow,
  output C_out
);

  wire adder_1_out, and_1_out, multiplexer_1_out, multiplexer_2_out, not_1_out, not_2_out, or_1_out;

  not not_1 (not_1_out, A);
  Multiplexer #(.enable("false")) multiplexer_1 (.in0(A), .in1(not_1_out), .out(multiplexer_1_out), .sel(A_invert));
  not not_2 (not_2_out, B);
  Multiplexer #(.enable("false")) multiplexer_2 (.in0(B), .in1(not_2_out), .out(multiplexer_2_out), .sel(B_Invert));
  and and_1 (and_1_out, multiplexer_1_out, multiplexer_2_out);
  or or_1 (or_1_out, multiplexer_1_out, multiplexer_2_out);
  Adder #(.width(1)) adder_1 (
    .a(multiplexer_1_out), .b(multiplexer_2_out), .out(adder_1_out), .cin(C_in), .cout(C_out));
  Multiplexer #(.select(2), .enable("false")) multiplexer_3 (
    .in0(and_1_out), .in1(or_1_out), .in2(adder_1_out), .in3(Less), .out(Result), .sel(Op_code));
  xor xor_1 (Overflow, C_in, C_out);
  xor xor_2 (Set, adder_1_out, Overflow);
endmodule

// 4 ALU
module _4_BIT_ALU (
  input  Less_0,
  input  A_invert,
  input  B_Invert,
  input  C_in,
  input  [1:0] Op_code,
  input  [3:0] A,
  input  [3:0] B,
  input  Less,
  output [3:0] out_9,
  output Set,
  output Overflow,
  output C_out
);

  wire n1_bit_alu_1_c_out, n1_bit_alu_2_c_out, n1_bit_alu_3_c_out;

  _1_BIT_ALU u_1_bit_alu_1 (
    .A(A[0]), .B(B[0]), .Less(Less_0), .A_invert(A_invert), .B_Invert(B_Invert), .C_in(C_in),
    .Op_code(Op_code), .C_out(n1_bit_alu_1_c_out), .Result(out_9[0]));  // open: Set, Overflow
  _1_BIT_ALU u_1_bit_alu_2 (
    .A(A[1]), .B(B[1]), .Less(Less), .A_invert(A_invert), .B_Invert(B_Invert), .C_in(n1_bit_alu_1_c_out),
    .Op_code(Op_code), .C_out(n1_bit_alu_2_c_out), .Result(out_9[1]));  // open: Set, Overflow
  _1_BIT_ALU u_1_bit_alu_3 (
    .A(A[2]), .B(B[2]), .Less(Less), .A_invert(A_invert), .B_Invert(B_Invert), .C_in(n1_bit_alu_2_c_out),
    .Op_code(Op_code), .C_out(n1_bit_alu_3_c_out), .Result(out_9[2]));  // open: Set, Overflow
  _1_BIT_ALU u_1_bit_alu_4 (
    .A(A[3]), .B(B[3]), .Less(Less), .A_invert(A_invert), .B_Invert(B_Invert), .C_in(n1_bit_alu_3_c_out),
    .Op_code(Op_code), .C_out(C_out), .Result(out_9[3]), .Set(Set), .Overflow(Overflow));
endmodule

// 16 ALU
module _16_BIT_ALU (
  input  Less_0,
  input  A_invert,
  input  B_Invert,
  input  C_in,
  input  [1:0] Op_code,
  input  [15:0] A,
  input  [15:0] B,
  input  Less,
  output [15:0] Result,
  output Set,
  output Overflow,
  output C_out
);

  wire n4_bit_alu_1_c_out, n4_bit_alu_2_c_out, n4_bit_alu_3_c_out;

  _4_BIT_ALU u_4_bit_alu_1 (
    .A(A[3:0]), .B(B[3:0]), .Less(Less), .Less_0(Less_0), .A_invert(A_invert), .B_Invert(B_Invert),
    .C_in(C_in), .Op_code(Op_code), .C_out(n4_bit_alu_1_c_out), .out_9(Result[3:0]));  // open: Set, Overflow
  _4_BIT_ALU u_4_bit_alu_2 (
    .A(A[7:4]), .B(B[7:4]), .Less(Less), .Less_0(Less), .A_invert(A_invert), .B_Invert(B_Invert),
    .C_in(n4_bit_alu_1_c_out), .Op_code(Op_code), .C_out(n4_bit_alu_2_c_out), .out_9(Result[7:4]));  // open: Set, Overflow
  _4_BIT_ALU u_4_bit_alu_3 (
    .A(A[11:8]), .B(B[11:8]), .Less(Less), .Less_0(Less), .A_invert(A_invert), .B_Invert(B_Invert),
    .C_in(n4_bit_alu_2_c_out), .Op_code(Op_code), .C_out(n4_bit_alu_3_c_out), .out_9(Result[11:8]));  // open: Set, Overflow
  _4_BIT_ALU u_4_bit_alu_4 (
    .A(A[15:12]), .B(B[15:12]), .Less(Less), .Less_0(Less), .A_invert(A_invert), .B_Invert(B_Invert),
    .C_in(n4_bit_alu_3_c_out), .Op_code(Op_code), .C_out(C_out), .out_9(Result[15:12]), .Set(Set),
    .Overflow(Overflow));
endmodule

module _32_BIT_ALU (
  input  [3:0] ALU_Opcode,
  input  [31:0] A,
  input  [31:0] B,
  output Zero_Dectector,
  output [31:0] Result,
  output Set,
  output Overflow
);

  wire n16_bit_alu_1_c_out, or_1_out;

  _16_BIT_ALU u_16_bit_alu_1 (
    .A(A[15:0]), .B(B[15:0]), .Less(1'b0), .Less_0(Set), .A_invert(ALU_Opcode[3]), .B_Invert(ALU_Opcode[2]),
    .C_in(ALU_Opcode[2]), .Op_code(ALU_Opcode[1:0]), .C_out(n16_bit_alu_1_c_out), .Result(Result[15:0]));  // open: Set, Overflow
  _16_BIT_ALU u_16_bit_alu_2 (
    .A(A[31:16]), .B(B[31:16]), .Less(1'b0), .Less_0(1'b0), .A_invert(ALU_Opcode[3]),
    .B_Invert(ALU_Opcode[2]), .C_in(n16_bit_alu_1_c_out), .Op_code(ALU_Opcode[1:0]), .Result(Result[31:16]),
    .Set(Set), .Overflow(Overflow));  // open: C_out
  or or_1 (or_1_out, Result[0], Result[1], Result[2], Result[3], Result[4], Result[5], Result[6], Result[7], Result[8], Result[9], Result[10], Result[11], Result[12], Result[13], Result[14], Result[15], Result[16], Result[17], Result[18], Result[19], Result[20], Result[21], Result[22], Result[23], Result[24], Result[25], Result[26], Result[27], Result[28], Result[29], Result[30], Result[31]);
  not not_1 (Zero_Dectector, or_1_out);

  // Notes on the sheet:
  //   A Negate
  //   B negate
endmodule

// 32 Reg
module _32_BIT_Register (
  input  [31:0] Data,
  input  W_Bar,
  input  Clock,
  output [31:0] Output
);

  wire or_1_out;

  or or_1 (or_1_out, ~W_Bar, Clock);  // OR_Gate
  D_Flip_Flop d_ff_1 (.clk(or_1_out), .D(Data[24]), .Q(Output[24]));  // open: Qn, preset, en, reset
  D_Flip_Flop d_ff_2 (.clk(or_1_out), .D(Data[25]), .Q(Output[25]));  // open: Qn, preset, en, reset
  D_Flip_Flop d_ff_3 (.clk(or_1_out), .D(Data[26]), .Q(Output[26]));  // open: Qn, preset, en, reset
  D_Flip_Flop d_ff_4 (.clk(or_1_out), .D(Data[27]), .Q(Output[27]));  // open: Qn, preset, en, reset
  D_Flip_Flop d_ff_5 (.clk(or_1_out), .D(Data[28]), .Q(Output[28]));  // open: Qn, preset, en, reset
  D_Flip_Flop d_ff_6 (.clk(or_1_out), .D(Data[29]), .Q(Output[29]));  // open: Qn, preset, en, reset
  D_Flip_Flop d_ff_7 (.clk(or_1_out), .D(Data[30]), .Q(Output[30]));  // open: Qn, preset, en, reset
  D_Flip_Flop d_ff_8 (.clk(or_1_out), .D(Data[31]), .Q(Output[31]));  // open: Qn, preset, en, reset
  D_Flip_Flop d_ff_9 (.clk(or_1_out), .D(Data[16]), .Q(Output[16]));  // open: Qn, preset, en, reset
  D_Flip_Flop d_ff_10 (.clk(or_1_out), .D(Data[17]), .Q(Output[17]));  // open: Qn, preset, en, reset
  D_Flip_Flop d_ff_11 (.clk(or_1_out), .D(Data[18]), .Q(Output[18]));  // open: Qn, preset, en, reset
  D_Flip_Flop d_ff_12 (.clk(or_1_out), .D(Data[19]), .Q(Output[19]));  // open: Qn, preset, en, reset
  D_Flip_Flop d_ff_13 (.clk(or_1_out), .D(Data[20]), .Q(Output[20]));  // open: Qn, preset, en, reset
  D_Flip_Flop d_ff_14 (.clk(or_1_out), .D(Data[21]), .Q(Output[21]));  // open: Qn, preset, en, reset
  D_Flip_Flop d_ff_15 (.clk(or_1_out), .D(Data[22]), .Q(Output[22]));  // open: Qn, preset, en, reset
  D_Flip_Flop d_ff_16 (.clk(or_1_out), .D(Data[23]), .Q(Output[23]));  // open: Qn, preset, en, reset
  D_Flip_Flop d_ff_17 (.clk(or_1_out), .D(Data[8]), .Q(Output[8]));  // open: Qn, preset, en, reset
  D_Flip_Flop d_ff_18 (.clk(or_1_out), .D(Data[9]), .Q(Output[9]));  // open: Qn, preset, en, reset
  D_Flip_Flop d_ff_19 (.clk(or_1_out), .D(Data[10]), .Q(Output[10]));  // open: Qn, preset, en, reset
  D_Flip_Flop d_ff_20 (.clk(or_1_out), .D(Data[11]), .Q(Output[11]));  // open: Qn, preset, en, reset
  D_Flip_Flop d_ff_21 (.clk(or_1_out), .D(Data[12]), .Q(Output[12]));  // open: Qn, preset, en, reset
  D_Flip_Flop d_ff_22 (.clk(or_1_out), .D(Data[13]), .Q(Output[13]));  // open: Qn, preset, en, reset
  D_Flip_Flop d_ff_23 (.clk(or_1_out), .D(Data[14]), .Q(Output[14]));  // open: Qn, preset, en, reset
  D_Flip_Flop d_ff_24 (.clk(or_1_out), .D(Data[15]), .Q(Output[15]));  // open: Qn, preset, en, reset
  D_Flip_Flop d_ff_25 (.clk(or_1_out), .D(Data[0]), .Q(Output[0]));  // open: Qn, preset, en, reset
  D_Flip_Flop d_ff_26 (.clk(or_1_out), .D(Data[1]), .Q(Output[1]));  // open: Qn, preset, en, reset
  D_Flip_Flop d_ff_27 (.clk(or_1_out), .D(Data[2]), .Q(Output[2]));  // open: Qn, preset, en, reset
  D_Flip_Flop d_ff_28 (.clk(or_1_out), .D(Data[3]), .Q(Output[3]));  // open: Qn, preset, en, reset
  D_Flip_Flop d_ff_29 (.clk(or_1_out), .D(Data[4]), .Q(Output[4]));  // open: Qn, preset, en, reset
  D_Flip_Flop d_ff_30 (.clk(or_1_out), .D(Data[5]), .Q(Output[5]));  // open: Qn, preset, en, reset
  D_Flip_Flop d_ff_31 (.clk(or_1_out), .D(Data[6]), .Q(Output[6]));  // open: Qn, preset, en, reset
  D_Flip_Flop d_ff_32 (.clk(or_1_out), .D(Data[7]), .Q(Output[7]));  // open: Qn, preset, en, reset
endmodule

module Register_File (
  input  Write_X,
  input  Clock,
  input  [4:0] Reg_Selector,
  input  [31:0] Data_to_Write,
  input  [4:0] Read_Reg_1,
  input  [4:0] Read_Reg_2,
  output [31:0] Read_Data_1,
  output [31:0] Read_Data_2
);

  wire and_1_out, and_2_out, and_3_out, and_4_out, and_5_out, and_6_out, and_7_out, and_8_out, and_9_out,
       and_10_out, and_11_out, and_12_out, and_13_out, and_14_out, and_15_out, and_16_out, and_17_out,
       and_18_out, and_19_out, and_20_out, and_21_out, and_22_out, and_23_out, and_24_out, and_25_out,
       and_26_out, and_27_out, and_28_out, and_29_out, and_30_out, and_31_out, and_32_out;
  wire [31:0] decoder_1_out0, n32_bit_register_1_output, n32_bit_register_2_output,
       n32_bit_register_3_output, n32_bit_register_4_output, n32_bit_register_5_output,
       n32_bit_register_6_output, n32_bit_register_7_output, n32_bit_register_8_output,
       n32_bit_register_9_output, n32_bit_register_10_output, n32_bit_register_11_output,
       n32_bit_register_12_output, n32_bit_register_13_output, n32_bit_register_14_output,
       n32_bit_register_15_output, n32_bit_register_16_output, n32_bit_register_17_output,
       n32_bit_register_18_output, n32_bit_register_19_output, n32_bit_register_20_output,
       n32_bit_register_21_output, n32_bit_register_22_output, n32_bit_register_23_output,
       n32_bit_register_24_output, n32_bit_register_25_output, n32_bit_register_26_output,
       n32_bit_register_27_output, n32_bit_register_28_output, n32_bit_register_29_output,
       n32_bit_register_30_output, n32_bit_register_31_output, n32_bit_register_32_output;

  Decoder #(.select(5), .enable("false")) decoder_1 (
    .out0(decoder_1_out0[0]), .out1(decoder_1_out0[1]), .out2(decoder_1_out0[2]), .out3(decoder_1_out0[3]),
    .out4(decoder_1_out0[4]), .out5(decoder_1_out0[5]), .out6(decoder_1_out0[6]), .out7(decoder_1_out0[7]),
    .out8(decoder_1_out0[8]), .out9(decoder_1_out0[9]), .out10(decoder_1_out0[10]),
    .out11(decoder_1_out0[11]), .out12(decoder_1_out0[12]), .out13(decoder_1_out0[13]),
    .out14(decoder_1_out0[14]), .out15(decoder_1_out0[15]), .out16(decoder_1_out0[16]),
    .out17(decoder_1_out0[17]), .out18(decoder_1_out0[18]), .out19(decoder_1_out0[19]),
    .out20(decoder_1_out0[20]), .out21(decoder_1_out0[21]), .out22(decoder_1_out0[22]),
    .out23(decoder_1_out0[23]), .out24(decoder_1_out0[24]), .out25(decoder_1_out0[25]),
    .out26(decoder_1_out0[26]), .out27(decoder_1_out0[27]), .out28(decoder_1_out0[28]),
    .out29(decoder_1_out0[29]), .out30(decoder_1_out0[30]), .out31(decoder_1_out0[31]), .sel(Reg_Selector));
  and and_1 (and_1_out, Write_X, decoder_1_out0[24]);
  and and_2 (and_2_out, Write_X, decoder_1_out0[25]);
  and and_3 (and_3_out, Write_X, decoder_1_out0[26]);
  and and_4 (and_4_out, Write_X, decoder_1_out0[27]);
  and and_5 (and_5_out, Write_X, decoder_1_out0[28]);
  and and_6 (and_6_out, Write_X, decoder_1_out0[29]);
  and and_7 (and_7_out, Write_X, decoder_1_out0[30]);
  and and_8 (and_8_out, Write_X, decoder_1_out0[31]);
  _32_BIT_Register u_32_bit_register_1 (
    .Data(Data_to_Write), .W_Bar(and_1_out), .Clock(Clock), .Output(n32_bit_register_1_output));
  _32_BIT_Register u_32_bit_register_2 (
    .Data(Data_to_Write), .W_Bar(and_2_out), .Clock(Clock), .Output(n32_bit_register_2_output));
  _32_BIT_Register u_32_bit_register_3 (
    .Data(Data_to_Write), .W_Bar(and_3_out), .Clock(Clock), .Output(n32_bit_register_3_output));
  _32_BIT_Register u_32_bit_register_4 (
    .Data(Data_to_Write), .W_Bar(and_4_out), .Clock(Clock), .Output(n32_bit_register_4_output));
  _32_BIT_Register u_32_bit_register_5 (
    .Data(Data_to_Write), .W_Bar(and_5_out), .Clock(Clock), .Output(n32_bit_register_5_output));
  _32_BIT_Register u_32_bit_register_6 (
    .Data(Data_to_Write), .W_Bar(and_6_out), .Clock(Clock), .Output(n32_bit_register_6_output));
  _32_BIT_Register u_32_bit_register_7 (
    .Data(Data_to_Write), .W_Bar(and_7_out), .Clock(Clock), .Output(n32_bit_register_7_output));
  _32_BIT_Register u_32_bit_register_8 (
    .Data(Data_to_Write), .W_Bar(and_8_out), .Clock(Clock), .Output(n32_bit_register_8_output));
  _32_BIT_Register u_32_bit_register_9 (
    .Data(Data_to_Write), .W_Bar(and_9_out), .Clock(Clock), .Output(n32_bit_register_9_output));
  and and_9 (and_9_out, Write_X, decoder_1_out0[16]);
  and and_10 (and_10_out, Write_X, decoder_1_out0[17]);
  _32_BIT_Register u_32_bit_register_10 (
    .Data(Data_to_Write), .W_Bar(and_10_out), .Clock(Clock), .Output(n32_bit_register_10_output));
  _32_BIT_Register u_32_bit_register_11 (
    .Data(Data_to_Write), .W_Bar(and_11_out), .Clock(Clock), .Output(n32_bit_register_11_output));
  and and_11 (and_11_out, Write_X, decoder_1_out0[18]);
  and and_12 (and_12_out, Write_X, decoder_1_out0[19]);
  _32_BIT_Register u_32_bit_register_12 (
    .Data(Data_to_Write), .W_Bar(and_12_out), .Clock(Clock), .Output(n32_bit_register_12_output));
  and and_13 (and_13_out, Write_X, decoder_1_out0[20]);
  _32_BIT_Register u_32_bit_register_13 (
    .Data(Data_to_Write), .W_Bar(and_13_out), .Clock(Clock), .Output(n32_bit_register_13_output));
  _32_BIT_Register u_32_bit_register_14 (
    .Data(Data_to_Write), .W_Bar(and_14_out), .Clock(Clock), .Output(n32_bit_register_14_output));
  and and_14 (and_14_out, Write_X, decoder_1_out0[21]);
  _32_BIT_Register u_32_bit_register_15 (
    .Data(Data_to_Write), .W_Bar(and_15_out), .Clock(Clock), .Output(n32_bit_register_15_output));
  and and_15 (and_15_out, Write_X, decoder_1_out0[22]);
  and and_16 (and_16_out, Write_X, decoder_1_out0[23]);
  _32_BIT_Register u_32_bit_register_16 (
    .Data(Data_to_Write), .W_Bar(and_16_out), .Clock(Clock), .Output(n32_bit_register_16_output));
  and and_17 (and_17_out, Write_X, decoder_1_out0[8]);
  and and_18 (and_18_out, Write_X, decoder_1_out0[9]);
  and and_19 (and_19_out, Write_X, decoder_1_out0[10]);
  and and_20 (and_20_out, Write_X, decoder_1_out0[11]);
  and and_21 (and_21_out, Write_X, decoder_1_out0[12]);
  and and_22 (and_22_out, Write_X, decoder_1_out0[13]);
  and and_23 (and_23_out, Write_X, decoder_1_out0[14]);
  and and_24 (and_24_out, Write_X, decoder_1_out0[15]);
  _32_BIT_Register u_32_bit_register_17 (
    .Data(Data_to_Write), .W_Bar(and_17_out), .Clock(Clock), .Output(n32_bit_register_17_output));
  _32_BIT_Register u_32_bit_register_18 (
    .Data(Data_to_Write), .W_Bar(and_18_out), .Clock(Clock), .Output(n32_bit_register_18_output));
  _32_BIT_Register u_32_bit_register_19 (
    .Data(Data_to_Write), .W_Bar(and_19_out), .Clock(Clock), .Output(n32_bit_register_19_output));
  _32_BIT_Register u_32_bit_register_20 (
    .Data(Data_to_Write), .W_Bar(and_20_out), .Clock(Clock), .Output(n32_bit_register_20_output));
  _32_BIT_Register u_32_bit_register_21 (
    .Data(Data_to_Write), .W_Bar(and_21_out), .Clock(Clock), .Output(n32_bit_register_21_output));
  _32_BIT_Register u_32_bit_register_22 (
    .Data(Data_to_Write), .W_Bar(and_22_out), .Clock(Clock), .Output(n32_bit_register_22_output));
  _32_BIT_Register u_32_bit_register_23 (
    .Data(Data_to_Write), .W_Bar(and_23_out), .Clock(Clock), .Output(n32_bit_register_23_output));
  _32_BIT_Register u_32_bit_register_24 (
    .Data(Data_to_Write), .W_Bar(and_24_out), .Clock(Clock), .Output(n32_bit_register_24_output));
  and and_25 (and_25_out, Write_X, decoder_1_out0[0]);
  and and_26 (and_26_out, Write_X, decoder_1_out0[1]);
  and and_27 (and_27_out, Write_X, decoder_1_out0[2]);
  and and_28 (and_28_out, Write_X, decoder_1_out0[3]);
  and and_29 (and_29_out, Write_X, decoder_1_out0[4]);
  and and_30 (and_30_out, Write_X, decoder_1_out0[5]);
  and and_31 (and_31_out, Write_X, decoder_1_out0[6]);
  and and_32 (and_32_out, Write_X, decoder_1_out0[7]);
  _32_BIT_Register u_32_bit_register_25 (
    .Data(Data_to_Write), .W_Bar(and_25_out), .Clock(Clock), .Output(n32_bit_register_25_output));
  _32_BIT_Register u_32_bit_register_26 (
    .Data(Data_to_Write), .W_Bar(and_26_out), .Clock(Clock), .Output(n32_bit_register_26_output));
  _32_BIT_Register u_32_bit_register_27 (
    .Data(Data_to_Write), .W_Bar(and_27_out), .Clock(Clock), .Output(n32_bit_register_27_output));
  _32_BIT_Register u_32_bit_register_28 (
    .Data(Data_to_Write), .W_Bar(and_28_out), .Clock(Clock), .Output(n32_bit_register_28_output));
  _32_BIT_Register u_32_bit_register_29 (
    .Data(Data_to_Write), .W_Bar(and_29_out), .Clock(Clock), .Output(n32_bit_register_29_output));
  _32_BIT_Register u_32_bit_register_30 (
    .Data(Data_to_Write), .W_Bar(and_30_out), .Clock(Clock), .Output(n32_bit_register_30_output));
  _32_BIT_Register u_32_bit_register_31 (
    .Data(Data_to_Write), .W_Bar(and_31_out), .Clock(Clock), .Output(n32_bit_register_31_output));
  _32_BIT_Register u_32_bit_register_32 (
    .Data(Data_to_Write), .W_Bar(and_32_out), .Clock(Clock), .Output(n32_bit_register_32_output));
  Multiplexer #(.select(5), .width(32), .enable("false")) multiplexer_1 (
    .in0(n32_bit_register_25_output), .in1(n32_bit_register_26_output), .in2(n32_bit_register_27_output),
    .in3(n32_bit_register_28_output), .in4(n32_bit_register_29_output), .in5(n32_bit_register_30_output),
    .in6(n32_bit_register_31_output), .in7(n32_bit_register_32_output), .in8(n32_bit_register_17_output),
    .in9(n32_bit_register_18_output), .in10(n32_bit_register_19_output), .in11(n32_bit_register_20_output),
    .in12(n32_bit_register_21_output), .in13(n32_bit_register_22_output), .in14(n32_bit_register_23_output),
    .in15(n32_bit_register_24_output), .in16(n32_bit_register_9_output), .in17(n32_bit_register_10_output),
    .in18(n32_bit_register_11_output), .in19(n32_bit_register_12_output), .in20(n32_bit_register_13_output),
    .in21(n32_bit_register_14_output), .in22(n32_bit_register_15_output), .in23(n32_bit_register_16_output),
    .in24(n32_bit_register_1_output), .in25(n32_bit_register_2_output), .in26(n32_bit_register_3_output),
    .in27(n32_bit_register_4_output), .in28(n32_bit_register_5_output), .in29(n32_bit_register_6_output),
    .in30(n32_bit_register_7_output), .in31(n32_bit_register_8_output), .out(Read_Data_1), .sel(Read_Reg_1));
  Multiplexer #(.select(5), .width(32), .enable("false")) multiplexer_2 (
    .in0(n32_bit_register_25_output), .in1(n32_bit_register_26_output), .in2(n32_bit_register_27_output),
    .in3(n32_bit_register_28_output), .in4(n32_bit_register_29_output), .in5(n32_bit_register_30_output),
    .in6(n32_bit_register_31_output), .in7(n32_bit_register_32_output), .in8(n32_bit_register_17_output),
    .in9(n32_bit_register_18_output), .in10(n32_bit_register_19_output), .in11(n32_bit_register_20_output),
    .in12(n32_bit_register_21_output), .in13(n32_bit_register_22_output), .in14(n32_bit_register_23_output),
    .in15(n32_bit_register_24_output), .in16(n32_bit_register_9_output), .in17(n32_bit_register_10_output),
    .in18(n32_bit_register_11_output), .in19(n32_bit_register_12_output), .in20(n32_bit_register_13_output),
    .in21(n32_bit_register_14_output), .in22(n32_bit_register_15_output), .in23(n32_bit_register_16_output),
    .in24(n32_bit_register_1_output), .in25(n32_bit_register_2_output), .in26(n32_bit_register_3_output),
    .in27(n32_bit_register_4_output), .in28(n32_bit_register_5_output), .in29(n32_bit_register_6_output),
    .in30(n32_bit_register_7_output), .in31(n32_bit_register_8_output), .out(Read_Data_2), .sel(Read_Reg_2));
endmodule

module Main_Control (
  input  [5:0] Opcode_31_26,
  output Reg_Dst,
  output ALU_Src,
  output MemtoReg,
  output Reg_Write,
  output Mem_Read,
  output Mem_Write,
  output Branch,
  output [1:0] ALU_Op
);

  and and_1 (ALU_Op[1], ~Opcode_31_26[5], ~Opcode_31_26[4], ~Opcode_31_26[3], ~Opcode_31_26[2], ~Opcode_31_26[1], ~Opcode_31_26[0]);  // AND_Gate
  and and_2 (Mem_Read, Opcode_31_26[5], ~Opcode_31_26[4], ~Opcode_31_26[3], ~Opcode_31_26[2], Opcode_31_26[1], Opcode_31_26[0]);  // AND_Gate
  and and_3 (Mem_Write, Opcode_31_26[5], ~Opcode_31_26[4], Opcode_31_26[3], ~Opcode_31_26[2], Opcode_31_26[1], Opcode_31_26[0]);  // AND_Gate
  and and_4 (ALU_Op[0], ~Opcode_31_26[5], ~Opcode_31_26[4], ~Opcode_31_26[3], Opcode_31_26[2], ~Opcode_31_26[1], ~Opcode_31_26[0]);  // AND_Gate
  or or_1 (ALU_Src, Mem_Write, Mem_Read);
  or or_2 (Reg_Write, Mem_Read, ALU_Op[1]);

  assign Branch = ALU_Op[0];
  assign MemtoReg = Mem_Read;
  assign Reg_Dst = ALU_Op[1];
endmodule

module Processor (
  input  Jump
);

  wire _32_ALU_zero_dectector, and_1_out, Clock_out, Control_alu_src, Control_branch, Control_mem_read,
       Control_mem_write, Control_memtoreg, Control_reg_dst, Control_reg_write;
  wire [1:0] Control_alu_op;
  wire [3:0] ALU_control_alucontrol, JTA_concat__4_bit_out;
  wire [4:0] Address_addr_out, AddressPC_addr_out, multiplexer_1_out;
  wire [25:0] SLL2_output;
  wire [27:0] SignExtend26_28_out_2;
  wire [31:0] _32_ALU_result, adder_1_out, adder_2_out, Data_Memory_read_data, JTA_concat_output,
       multiplexer_2_out, multiplexer_3_out, multiplexer_4_out, multiplexer_5_out, program_counter_1_pcout,
       RegFile_read_data_1, RegFile_read_data_2, rom_1_data, Sign_Extend_16_32_output, SLL2_2_output;

  Program_Counter program_counter_1 (.PCin(multiplexer_4_out), .Clock(Clock_out), .PCout(program_counter_1_pcout));
  Address_from_PC AddressPC (.Addr_In(program_counter_1_pcout), .Addr_Out(AddressPC_addr_out));
  Shift_left_26_bits SLL2 (.Input(rom_1_data[25:0]), .Output(SLL2_output));
  Clock Clock (.out(Clock_out));
  Adder #(.width(32)) adder_1 (.a(program_counter_1_pcout), .b(32'h4), .out(adder_1_out));  // open: cin, cout
  ROM #(.addrWidth(5), .dataWidth(32)) rom_1 (.addr(AddressPC_addr_out), .data(rom_1_data));  // open: sel
  Sign_Extend_26_28 SignExtend26_28 (.in_1(SLL2_output), .out_2(SignExtend26_28_out_2));
  _32_4 JTA_concat (.Input(adder_1_out), ._4_Bit_out(JTA_concat__4_bit_out), .Output(JTA_concat_output));
  Main_Control Control (
    .Opcode_31_26(rom_1_data[31:26]), .Reg_Dst(Control_reg_dst), .ALU_Src(Control_alu_src),
    .MemtoReg(Control_memtoreg), .Reg_Write(Control_reg_write), .Mem_Read(Control_mem_read),
    .Mem_Write(Control_mem_write), .Branch(Control_branch), .ALU_Op(Control_alu_op));
  Sign_Extend_16_32 Sign_Extend_16_32 (.Input(rom_1_data[15:0]), .Output(Sign_Extend_16_32_output));
  Multiplexer #(.width(5), .enable("false")) multiplexer_1 (
    .in0(rom_1_data[20:16]), .in1(rom_1_data[15:11]), .out(multiplexer_1_out), .sel(Control_reg_dst));
  Register_File RegFile (
    .Write_X(Control_reg_write), .Clock(Clock_out), .Reg_Selector(multiplexer_1_out),
    .Data_to_Write(multiplexer_5_out), .Read_Reg_1(rom_1_data[25:21]), .Read_Reg_2(rom_1_data[20:16]),
    .Read_Data_1(RegFile_read_data_1), .Read_Data_2(RegFile_read_data_2));
  Multiplexer #(.width(32), .enable("false")) multiplexer_2 (
    .in0(RegFile_read_data_2), .in1(Sign_Extend_16_32_output), .out(multiplexer_2_out), .sel(Control_alu_src));
  ALU_Control ALU_control (.ALUop(Control_alu_op), .F_5_0(rom_1_data[5:0]), .AluControl(ALU_control_alucontrol));
  _32_BIT_ALU _32_ALU (
    .A(RegFile_read_data_1), .B(multiplexer_2_out), .ALU_Opcode(ALU_control_alucontrol),
    .Zero_Dectector(_32_ALU_zero_dectector), .Result(_32_ALU_result));  // open: Set, Overflow
  Left_Shift_by_2 SLL2_2 (.in_1(Sign_Extend_16_32_output), .Output(SLL2_2_output));
  and and_1 (and_1_out, Control_branch, _32_ALU_zero_dectector);
  Address_from_PC Address (.Addr_In(_32_ALU_result), .Addr_Out(Address_addr_out));
  Adder #(.width(32)) adder_2 (.a(JTA_concat_output), .b(SLL2_2_output), .out(adder_2_out));  // open: cin, cout
  Data_Memory Data_Memory (
    .Address(Address_addr_out), .Data(RegFile_read_data_2), .Mem_Write(Control_mem_write),
    .Mem_Read(Control_mem_read), .Read_Data(Data_Memory_read_data));
  Multiplexer #(.width(32), .enable("false")) multiplexer_3 (
    .in0(JTA_concat_output), .in1(adder_2_out), .out(multiplexer_3_out), .sel(and_1_out));
  Multiplexer #(.width(32), .enable("false")) multiplexer_4 (
    .in0(multiplexer_3_out), .in1({JTA_concat__4_bit_out, SignExtend26_28_out_2}), .out(multiplexer_4_out),
    .sel(Jump));
  Multiplexer #(.width(32), .enable("false")) multiplexer_5 (
    .in0(_32_ALU_result), .in1(Data_Memory_read_data), .out(multiplexer_5_out), .sel(Control_memtoreg));

  // Notes on the sheet:
  //   contents of rom_1 (hex, n*v repeats v):
  //   22 8c010000 8c020004 8c030008 842022 822020 43282a 10a00002 411020 1000fffb ac040000 1000ffff
endmodule

module ALU_Control (
  input  [1:0] ALUop,
  input  [5:0] F_5_0,
  output [3:0] AluControl
);

  wire and_1_out, not_1_out, not_2_out, or_1_out;

  or or_1 (or_1_out, F_5_0[3], F_5_0[0]);
  and and_1 (and_1_out, ALUop[1], F_5_0[1]);
  and and_2 (AluControl[0], ALUop[1], or_1_out);
  not not_1 (not_1_out, ALUop[1]);
  not not_2 (not_2_out, F_5_0[2]);
  or or_2 (AluControl[2], ALUop[0], and_1_out);
  or or_3 (AluControl[1], not_1_out, not_2_out);

  assign AluControl[3] = 1'b0;

  // Notes on the sheet:
  //   ALU1
  //   ALU0
  //   B negate
  //   Op1
  //   Op0
endmodule

// IM
module Instruction_Memory (
  input  [4:0] Address,
  output [31:0] Instruction
);

  ROM #(.addrWidth(5), .dataWidth(32)) rom_1 (.addr(Address), .data(Instruction));  // open: sel
endmodule

module Data_Memory (
  input  Mem_Write,
  input  Mem_Read,
  input  [4:0] Address,
  input  [31:0] Data,
  output [31:0] Read_Data
);

  wire clock_1_out;

  Clock clock_1 (.out(clock_1_out));
  RAM #(.addrWidth(5), .dataWidth(32), .bus("separate")) ram_1 (
    .addr(Address), .din(Data), .data(Read_Data), .str(Mem_Write), .clk(clock_1_out), .ld(Mem_Read));  // open: sel, clr
endmodule

module Sign_Extend_16_32 (
  input  [15:0] Input,
  output [31:0] Output
);


  assign Output = {{16{1'b0}}, Input};
endmodule

module Left_Shift_by_2 (
  input  [31:0] in_1,
  output [31:0] Output
);


  assign Output = {in_1[29:0], 2'b00};
endmodule

// PC
module Program_Counter (
  input  [31:0] PCin,
  input  Clock,
  output [31:0] PCout
);

  Register #(.width(32)) register_1 (.D(PCin), .Q(PCout), .clk(Clock));  // open: en, clr
endmodule

// SL26
module Shift_Left_26 (
  input  [25:0] in_1,
  output [25:0] out_2
);


  assign out_2 = {in_1[23:0], 2'b00};
endmodule

module Sign_Extend_26_28 (
  input  [25:0] in_1,
  output [27:0] out_2
);


  assign out_2 = {2'b00, in_1};
endmodule

module Address_from_PC (
  input  [31:0] Addr_In,
  output [4:0] Addr_Out
);


  assign Addr_Out = Addr_In[6:2];
endmodule

module Shift_left_26_bits (
  input  [25:0] Input,
  output [25:0] Output
);


  assign Output = {Input[23:0], 2'b00};
endmodule

module _32_4 (
  input  [31:0] Input,
  output [3:0] _4_Bit_out,
  output [31:0] Output
);


  assign _4_Bit_out = Input[31:28];
  assign Output = Input;
endmodule

module MainControl2 (
  input  [5:0] Inpute,
  output RegDST,
  output ALU_Src,
  output Mem_To_Reg,
  output Reg_Write,
  output Mem_Read,
  output Mem_Write,
  output Branch,
  output [1:0] ALU_OP
);

  wire and_5_out;

  and and_1 (ALU_OP[1], ~Inpute[0], ~Inpute[1], ~Inpute[2], ~Inpute[3], ~Inpute[4], ~Inpute[5]);  // AND_Gate
  and and_2 (Mem_Read, Inpute[0], Inpute[1], ~Inpute[2], ~Inpute[3], ~Inpute[4], Inpute[5]);  // AND_Gate
  and and_3 (Mem_Write, Inpute[0], Inpute[1], ~Inpute[2], Inpute[3], ~Inpute[4], Inpute[5]);  // AND_Gate
  and and_4 (ALU_OP[0], ~Inpute[0], ~Inpute[1], Inpute[2], ~Inpute[3], ~Inpute[4], ~Inpute[5]);  // AND_Gate
  and and_5 (and_5_out, ~Inpute[0], ~Inpute[1], ~Inpute[2], Inpute[3], ~Inpute[4], ~Inpute[5]);  // AND_Gate
  or or_1 (ALU_Src, and_5_out, Mem_Read, Mem_Write);
  or or_2 (Reg_Write, and_5_out, ALU_OP[1], Mem_Read);

  assign Branch = ALU_OP[0];
  assign Mem_To_Reg = Mem_Read;
  assign RegDST = ALU_OP[1];
endmodule
